# Fritzing sketch smartSecurityIOT (saved by Fritzing 0.9.4)
breadboards: 1

parts:
  Raspberry_Pi_1 = Raspberry Pi 3 [part_number=RPI-3-V1.2]
  Componente1 = SRF05 Ultrasonic Rangefinder
  R1 = Resistor [tolerance=±5% resistance=220 package=THT]
  LED1 = LED - 5mm [color="Green (565nm)" package="5 mm [THT]"]

nets:
  N1: Raspberry_Pi_1.GPIO4, Componente1.Trig
  GND: Raspberry_Pi_1.GND, Componente1.GND, R1.Pin_1
  N2: Raspberry_Pi_1.GPIO17, Componente1.Echo
  N3: Raspberry_Pi_1.GPIO14, LED1.cathode
  5V: Raspberry_Pi_1.5V, Componente1.VCC
  N4: R1.Pin_0, LED1.anode
